# Fritzing sketch cabane_minou (saved by Fritzing 0.9.4)
circuit board: 9.25763cm x 7.32976cm
breadboards: 1

parts:
  R2 = Resistor [tolerance=±5% resistance=10k package=THT]
  R4 = Resistor [tolerance=±5% resistance=10k package=THT]
  R7 = Resistor [tolerance=±5% resistance=220 package=THT]
  D1 = Schottky Diode [part_number=1N5817 package="300 mil [THT]"]
  R8 = Resistor [tolerance=±5% resistance=50 package=THT]
  R9 = Resistor [tolerance=±5% resistance=220 package=THT]
  R10 = Resistor [tolerance=±5% resistance=220 package=THT]
  R11 = Resistor [tolerance=±5% resistance=10k package=THT]
  D2 = Schottky Diode [part_number=1N5817 package="300 mil [THT]"]
  R12 = Resistor [tolerance=±5% resistance=50 package=THT]
  R13 = Resistor [tolerance=±5% resistance=10k package=THT]
  D3 = Schottky Diode [part_number=1N5817 package="300 mil [THT]"]
  R14 = Resistor [tolerance=±5% resistance=10k package=THT]
  D4 = Schottky Diode [part_number=1N5817 package="300 mil [THT]"]
  R15 = Resistor [tolerance=±5% resistance=50 package=THT]
  R16 = Resistor [tolerance=±5% resistance=50 package=THT]
  J1 = Camdenboss CTB0158-11 [part_number=CTB0158-11 package=THT]
  U2 = DIODE-ZENER [package=diode-zener]
  R17 = Resistor [tolerance=±5% resistance=10k package=THT]
  R18 = Resistor [tolerance=±5% resistance=10k package=THT]
  JP1 = Header 6 [package=molex-1x6-ra]
  U3 = ESP8266 NodeMCU LoLin module

nets:
  3.3V: R2.Pin_0, R4.Pin_0, D1.cathode, R11.Pin_0, D2.cathode, R13.Pin_0, D3.cathode, R14.Pin_0, D4.cathode, R17.Pin_0, JP1.6, U3.3V3
  N1: R2.Pin_1, D1.anode, R8.Pin_0, U3.D1
  N2: R4.Pin_1, J1.pin5, U3.D5
  N3: R7.Pin_0, U3.D2
  N4: R7.Pin_1, J1.pin3
  N5: R8.Pin_1, J1.pin2
  N6: R9.Pin_0, U3.D4
  N7: R9.Pin_1, J1.pin4
  N8: R10.Pin_0, U3.D6
  N9: R10.Pin_1, J1.pin6
  N10: R11.Pin_1, D2.anode, R12.Pin_0, U3.D7
  N11: R12.Pin_1, J1.pin7
  N12: R13.Pin_1, D3.anode, R16.Pin_0, U3.S3
  N13: R14.Pin_1, D4.anode, R15.Pin_0, U3.S2
  N14: R15.Pin_1, J1.pin8
  N15: R16.Pin_1, J1.pin9
  5V: J1.pin1, U3.Vin
  N16: J1.pin10, R18.Pin_1, U3.A0
  GND: J1.pin11, U2.A, JP1.1, U3.GND
  N17: U2.C, R17.Pin_1, R18.Pin_0
  N18: JP1.2, U3.SK
  N19: JP1.3, U3.S0
  N20: JP1.4, U3.SC
  N21: JP1.5, U3.S1

custom parts:
  ESP8266 NodeMCU LoLin module: ESP8266 based NodeMCU
